# Fritzing sketch ejemplo (saved by Fritzing 0.9.3b)
circuit board: 8.46667cm x 5.64444cm
breadboards: 1

parts:
  C2 = Ceramic Capacitor [capacitance=100nF package="100 mil [THT, multilayer]"]
  PIC_16F877A1 = PIC 16F877A [package=THT]
  C3 = Ceramic Capacitor [capacitance=100nF package="100 mil [THT, multilayer]"]
  XTAL1 = Crystal [frequency="16 Mhz" package=THT]
  S2 = Momentary Switch [package=ksa_sealed_tac_switch]
  R1 = Resistor [tolerance=±5% resistance=220 package=THT]
  LED1 = LED - 5mm [color="Red (633nm)" package="5 mm [THT]"]
  R2 = Resistor [tolerance=±5% resistance=220 package=THT]
  Power_plug1 = Power plug
  R3 = Resistor [tolerance=±5% resistance=220 package=THT]
  S4 = Momentary Switch [package=ksa_sealed_tac_switch]

nets:
  N1: C2.0, PIC_16F877A1.VSS#11, C3.1, S2.4, LED1.cathode, Power_plug1.GND, R3.Pin_0
  N2: C2.1, PIC_16F877A1.OSC1/CLKIN, XTAL1.pin_0
  N3: PIC_16F877A1.MCLR, S2.2, R1.Pin_0
  N4: PIC_16F877A1.VDD#10, R1.Pin_1, Power_plug1.VCC, S4.1
  N5: PIC_16F877A1.OSC2/CLKOUT, C3.0, XTAL1.pin_1
  N6: PIC_16F877A1.RB0/INT, R3.Pin_1, S4.3
  N7: PIC_16F877A1.RB7, R2.Pin_1
  N8: LED1.anode, R2.Pin_0
