# Fritzing sketch ejemplo (saved by Fritzing 0.9.3b)
breadboards: 1

parts:
  C2 = Ceramic Capacitor [capacitance=22pF package="100 mil [THT, multilayer]"]
  PIC_16F877A1 = PIC 16F877A [package=THT]
  C3 = Ceramic Capacitor [capacitance=22pF package="100 mil [THT, multilayer]"]
  XTAL1 = Crystal [frequency="16 Mhz" package=THT]
  S2 = Momentary Switch [package=ksa_sealed_tac_switch]
  R1 = Resistor [tolerance=±5% resistance=220 package=THT]
  R5 = Resistor [tolerance=±5% resistance=220 package=THT]
  R6 = Resistor [tolerance=±5% resistance=220 package=THT]
  R7 = Resistor [tolerance=±5% resistance=220 package=THT]
  R14 = Resistor [tolerance=±5% resistance=220 package=THT]
  R15 = Resistor [tolerance=±5% resistance=220 package=THT]
  R16 = Resistor [tolerance=±5% resistance=220 package=THT]
  R17 = Resistor [tolerance=±5% resistance=220 package=THT]
  Power_plug1 = Power plug
  U1 = 7-SEGMENT-DISPLAY [package=7-segment-display]

nets:
  N1: C2.0, PIC_16F877A1.VSS#11, C3.1, S2.4, Power_plug1.GND
  N2: C2.1, PIC_16F877A1.OSC1/CLKIN, XTAL1.pin_0
  N3: PIC_16F877A1.MCLR, S2.2, R1.Pin_0
  N4: PIC_16F877A1.VDD#10, R1.Pin_1, Power_plug1.VCC, U1.F
  N5: PIC_16F877A1.OSC2/CLKOUT, C3.0, XTAL1.pin_1
  N6: PIC_16F877A1.RB0/INT, R17.Pin_0
  N7: PIC_16F877A1.RB1, R16.Pin_0
  N8: PIC_16F877A1.RB2, R6.Pin_0
  N9: PIC_16F877A1.RB3, R5.Pin_0
  N10: PIC_16F877A1.RB4, R7.Pin_0
  N11: PIC_16F877A1.RB5, R15.Pin_0
  N12: PIC_16F877A1.RB6, R14.Pin_0
  N13: R5.Pin_1, U1.G1
  N14: R6.Pin_1, U1.DP
  N15: R7.Pin_1, U1.D
  N16: R14.Pin_1, U1.E
  N17: R15.Pin_1, U1.G
  N18: R16.Pin_1, U1.A
  N19: R17.Pin_1, U1.G2
