# Fritzing sketch ejemplo (saved by Fritzing 0.9.3b)
breadboards: 1

parts:
  C2 = Ceramic Capacitor [capacitance=100nF package="100 mil [THT, multilayer]"]
  PIC_16F877A1 = PIC 16F877A [package=THT]
  C3 = Ceramic Capacitor [capacitance=100nF package="100 mil [THT, multilayer]"]
  XTAL1 = Crystal [frequency="16 Mhz" package=THT]
  S2 = Momentary Switch [package=ksa_sealed_tac_switch]
  R1 = Resistor [tolerance=±5% resistance=220 package=THT]
  U1 = 7-SEGMENT-DISPLAY [package=7-segment-display]
  R5 = Resistor [tolerance=±5% resistance=220 package=THT]
  R6 = Resistor [tolerance=±5% resistance=220 package=THT]
  R7 = Resistor [tolerance=±5% resistance=220 package=THT]
  S3 = Momentary Switch [package=ksa_sealed_tac_switch]
  S4 = Momentary Switch [package=ksa_sealed_tac_switch]
  R12 = Resistor [tolerance=±5% resistance=220 package=THT]
  R13 = Resistor [tolerance=±5% resistance=220 package=THT]
  R14 = Resistor [tolerance=±5% resistance=220 package=THT]
  R15 = Resistor [tolerance=±5% resistance=220 package=THT]
  R16 = Resistor [tolerance=±5% resistance=220 package=THT]
  R17 = Resistor [tolerance=±5% resistance=220 package=THT]
  Power_plug1 = Power plug

nets:
  N1: C2.0, PIC_16F877A1.VSS#11, C3.1, S2.4, R12.Pin_0, R13.Pin_0, Power_plug1.GND
  N2: C2.1, PIC_16F877A1.OSC1/CLKIN, XTAL1.pin_0
  N3: PIC_16F877A1.MCLR, S2.2, R1.Pin_0
  N4: PIC_16F877A1.VDD#10, R1.Pin_1, U1.F, S3.3, S4.3, Power_plug1.VCC
  N5: PIC_16F877A1.OSC2/CLKOUT, C3.0, XTAL1.pin_1
  N6: PIC_16F877A1.RD0/PSP0, S4.1, R12.Pin_1
  N7: PIC_16F877A1.RD1/PSP1, S3.1, R13.Pin_1
  N8: PIC_16F877A1.RB0/INT, R17.Pin_0
  N9: PIC_16F877A1.RB1, R16.Pin_0
  N10: PIC_16F877A1.RB2, R6.Pin_0
  N11: PIC_16F877A1.RB3, R5.Pin_0
  N12: PIC_16F877A1.RB4, R7.Pin_0
  N13: PIC_16F877A1.RB5, R15.Pin_0
  N14: PIC_16F877A1.RB6, R14.Pin_0
  N15: U1.E, R14.Pin_1
  N16: U1.D, R7.Pin_1
  N17: U1.G1, R5.Pin_1
  N18: U1.DP, R6.Pin_1
  N19: U1.A, R16.Pin_1
  N20: U1.G2, R17.Pin_1
  N21: U1.G, R15.Pin_1
