# Fritzing sketch proyecto (saved by Fritzing 0.9.3b)
circuit board: 8.46667cm x 5.64444cm
breadboards: 1

parts:
  C2 = Ceramic Capacitor [capacitance=100nF package="100 mil [THT, multilayer]"]
  C3 = Ceramic Capacitor [capacitance=100nF package="100 mil [THT, multilayer]"]
  XTAL1 = Crystal [frequency="16 Mhz" package=THT]
  S2 = Momentary Switch [package=ksa_sealed_tac_switch]
  R1 = Resistor [tolerance=±5% resistance=220 package=THT]
  Disp1 = LBT2088AH [part_number=LBT2088AH]
  PIC_16F877A1 = PIC 16F877A [package=THT]
  U1 = 74HC595 [package="DIP16 [THT]"]

nets:
  N1: C2.0, C3.1, S2.4, PIC_16F877A1.VSS#11, U1.GND, U1.OE
  N2: C2.1, XTAL1.pin_0, PIC_16F877A1.OSC1/CLKIN
  N3: C3.0, XTAL1.pin_1, PIC_16F877A1.OSC2/CLKOUT
  N4: S2.2, R1.Pin_0, PIC_16F877A1.MCLR
  N5: R1.Pin_1, PIC_16F877A1.VDD#10, U1.MR, U1.VCC
  N6: Disp1.pin1, U1.Q0
  N7: Disp1.pin2, U1.Q1
  N8: Disp1.pin_3, U1.Q2
  N9: Disp1.pin_4, U1.Q3
  N10: Disp1.pin_5, U1.Q4
  N11: Disp1.pin_6, U1.Q5
  N12: Disp1.pin_7, U1.Q6
  N13: Disp1.pin_8, U1.Q7
  N14: Disp1.pin_9, PIC_16F877A1.RC7/RX/DT
  N15: Disp1.pin_10, PIC_16F877A1.RC6/TX/CK
  N16: Disp1.pin_11, PIC_16F877A1.RC5
  N17: Disp1.pin_12, PIC_16F877A1.RC4
  N18: Disp1.pin_13, PIC_16F877A1.RD3/PSP3
  N19: Disp1.pin_14, PIC_16F877A1.RD2/PSP2
  N20: Disp1.pin_15, PIC_16F877A1.RD1/PSP1
  N21: Disp1.pin_16, PIC_16F877A1.RD0/PSP0
  N22: PIC_16F877A1.RD6/PSP6, U1.SH_CP
  N23: PIC_16F877A1.RD7/PSP7, U1.DS
  N24: PIC_16F877A1.VSS#30, U1.ST_CP
