# Fritzing sketch ejemplo5 (saved by Fritzing 0.9.3b)
circuit board: 8.46667cm x 5.64444cm
breadboards: 1

parts:
  C2 = Ceramic Capacitor [capacitance=100nF package="100 mil [THT, multilayer]"]
  PIC_16F877A1 = PIC 16F877A [package=THT]
  C3 = Ceramic Capacitor [capacitance=100nF package="100 mil [THT, multilayer]"]
  XTAL1 = Crystal [frequency="16 Mhz" package=THT]
  S2 = Momentary Switch [package=ksa_sealed_tac_switch]
  R1 = Resistor [tolerance=±5% resistance=220 package=THT]
  LCD1 = LCD screen
  Matrix_keypad2 = KEYPAD 4x4
  R2 = Rotary Potentiometer (Small) [maximum_resistance=100kΩ package=THT]

nets:
  N1: C2.0, PIC_16F877A1.VSS#11, C3.1, S2.4, LCD1.VSS, LCD1.LED-, R2.leg1
  N2: C2.1, PIC_16F877A1.OSC1/CLKIN, XTAL1.pin_0
  N3: PIC_16F877A1.MCLR, S2.2, R1.Pin_0
  N4: PIC_16F877A1.VDD#10, R1.Pin_1, LCD1.VDD, LCD1.LED+, R2.leg2
  N5: PIC_16F877A1.OSC2/CLKOUT, C3.0, XTAL1.pin_1
  N6: PIC_16F877A1.RD0/PSP0, LCD1.E
  N7: PIC_16F877A1.RD1/PSP1, LCD1.RS
  N8: PIC_16F877A1.RD2/PSP2, LCD1.R/W
  N9: PIC_16F877A1.RD4/PSP4, LCD1.DB4
  N10: PIC_16F877A1.RD5/PSP5, LCD1.DB5
  N11: PIC_16F877A1.RD6/PSP6, LCD1.DB6
  N12: PIC_16F877A1.RD7/PSP7, LCD1.DB7
  N13: PIC_16F877A1.RB0/INT, Matrix_keypad2.col1
  N14: PIC_16F877A1.RB1, Matrix_keypad2.col2
  N15: PIC_16F877A1.RB2, Matrix_keypad2.col3
  N16: PIC_16F877A1.RB3, Matrix_keypad2.col4
  N17: PIC_16F877A1.RB4, Matrix_keypad2.row1
  N18: PIC_16F877A1.RB5, Matrix_keypad2.row2
  N19: PIC_16F877A1.RB6, Matrix_keypad2.row3
  N20: PIC_16F877A1.RB7, Matrix_keypad2.row4
  N21: LCD1.V0, R2.wiper

custom parts:
  KEYPAD 4x4: Matrix keypad 16 buttons, 4 rows x 4 columns
