# Fritzing sketch ejemplo6 (saved by Fritzing 0.9.3b)
circuit board: 8.46667cm x 5.64444cm
breadboards: 1

parts:
  C2 = Ceramic Capacitor [capacitance=100nF package="100 mil [THT, multilayer]"]
  PIC_16F877A1 = PIC 16F877A [package=THT]
  C3 = Ceramic Capacitor [capacitance=100nF package="100 mil [THT, multilayer]"]
  XTAL1 = Crystal [frequency="16 Mhz" package=THT]
  S2 = Momentary Switch [package=ksa_sealed_tac_switch]
  R1 = Resistor [tolerance=±5% resistance=220 package=THT]
  GLCD_128x1 = 128 x 64 Graphic LCD

nets:
  N1: C2.0, PIC_16F877A1.VSS#11, C3.1, S2.4, GLCD_128x1.1_Vss, GLCD_128x1.20_K(-)
  N2: C2.1, PIC_16F877A1.OSC1/CLKIN, XTAL1.pin_0
  N3: PIC_16F877A1.MCLR, S2.2, R1.Pin_0
  N4: PIC_16F877A1.VDD#10, R1.Pin_1, GLCD_128x1.2_Vdd, GLCD_128x1.3_Vo, GLCD_128x1.19_A(+)
  N5: PIC_16F877A1.OSC2/CLKOUT, C3.0, XTAL1.pin_1
  N6: PIC_16F877A1.RC0, GLCD_128x1.17_RST
  N7: PIC_16F877A1.RD0/PSP0, GLCD_128x1.7_DB0
  N8: PIC_16F877A1.RD1/PSP1, GLCD_128x1.8_DB1
  N9: PIC_16F877A1.RD2/PSP2, GLCD_128x1.9_BD2
  N10: PIC_16F877A1.RD3/PSP3, GLCD_128x1.10_DB3
  N11: PIC_16F877A1.RD4/PSP4, GLCD_128x1.11_DB4
  N12: PIC_16F877A1.RD5/PSP5, GLCD_128x1.12_DB5
  N13: PIC_16F877A1.RD6/PSP6, GLCD_128x1.13_DB6
  N14: PIC_16F877A1.RD7/PSP7, GLCD_128x1.14_DB7
  N15: PIC_16F877A1.RB0/INT, GLCD_128x1.15_CS1
  N16: PIC_16F877A1.RB1, GLCD_128x1.16_CS2
  N17: PIC_16F877A1.RB2, GLCD_128x1.4_D/I
  N18: PIC_16F877A1.RB4, GLCD_128x1.5_R/W
  N19: PIC_16F877A1.RB5, GLCD_128x1.6_Enable
