# Fritzing sketch ejemplo3 (saved by Fritzing 0.9.3b)
circuit board: 8.46667cm x 5.64444cm
breadboards: 1

parts:
  C2 = Ceramic Capacitor [capacitance=100nF package="100 mil [THT, multilayer]"]
  PIC_16F877A1 = PIC 16F877A [package=THT]
  C3 = Ceramic Capacitor [capacitance=100nF package="100 mil [THT, multilayer]"]
  XTAL1 = Crystal [frequency="16 Mhz" package=THT]
  S2 = Momentary Switch [package=ksa_sealed_tac_switch]
  R1 = Resistor [tolerance=±5% resistance=220 package=THT]
  LCD1 = LCD screen
  R2 = Rotary Potentiometer (Small) [maximum_resistance=100kΩ package=THT]
  R3 = Rotary Potentiometer (Large) [maximum_resistance=100kΩ package=THT]
  J1 = Basic Servo

nets:
  VSS: C2.0, PIC_16F877A1.VSS#11, C3.1, S2.4, LCD1.VSS, LCD1.LED-, R2.leg1, J1.gnd
  N1: C2.1, PIC_16F877A1.OSC1/CLKIN, XTAL1.pin_0
  N2: PIC_16F877A1.MCLR, S2.2, R1.Pin_0
  N3: PIC_16F877A1.RA0/AN0, R3.wiper
  N4: PIC_16F877A1.RA2/AN2, LCD1.DB5
  N5: PIC_16F877A1.RA3/AN3, LCD1.DB4
  N6: PIC_16F877A1.RA5/AN4/SS, LCD1.DB6
  VDD: PIC_16F877A1.VDD#10, R1.Pin_1, LCD1.VDD, LCD1.LED+, R2.leg2, J1.vcc
  N7: PIC_16F877A1.OSC2/CLKOUT, C3.0, XTAL1.pin_1
  N8: PIC_16F877A1.RC2, J1.pulse
  N9: PIC_16F877A1.RD0/PSP0, LCD1.E
  N10: PIC_16F877A1.RD1/PSP1, LCD1.RS
  N11: PIC_16F877A1.RD2/PSP2, LCD1.R/W
  N12: PIC_16F877A1.RD7/PSP7, LCD1.DB7
  N13: LCD1.V0, R2.wiper
