# Fritzing sketch ejemplo2 (saved by Fritzing 0.9.3b)
circuit board: 8.46667cm x 5.64444cm
breadboards: 1

parts:
  PIC_16F877A1 = PIC 16F877A [package=THT]
  S2 = Momentary Switch [package=ksa_sealed_tac_switch]
  R1 = Resistor [tolerance=±5% resistance=220 package=THT]
  Componente1 = FTDI Basic Programmer
  Componente2 = Thumb Joystick

nets:
  N1: PIC_16F877A1.MCLR, S2.2, R1.Pin_0
  N2: PIC_16F877A1.RA0/AN0, Componente2.VERT
  N3: PIC_16F877A1.RA1/AN1, Componente2.HORZ
  N4: PIC_16F877A1.VDD#10, R1.Pin_1, Componente2.VCC
  N5: PIC_16F877A1.VSS#11, S2.4, Componente2.GND
  N6: PIC_16F877A1.RC6/TX/CK, Componente1.RXI
  N7: PIC_16F877A1.RC7/RX/DT, Componente1.TXO
